// Logisim project 4-bit Full Adder.circ as structural Verilog: 6 circuits, main circuit main
module main (
  input  in_1,
  input  in_2
);


  // Notes on the sheet:
  //   cs31 lab3, part 1
  //   Julian Segert, Ziting Shen
endmodule

module XOR (
  input  X,
  input  Y,
  output out_3
);

  wire and_1_out, not_1_out, or_1_out;

  or or_1 (or_1_out, X, Y);
  and and_1 (and_1_out, X, Y);
  not not_1 (not_1_out, and_1_out);
  and and_2 (out_3, or_1_out, not_1_out);

  // Notes on the sheet:
  //   This is an XOR operator. It takes two 1-bit values and outputs a 1-bit boolean value.
endmodule

module fulladder (
  input  X,
  input  Y,
  input  CarryIn,
  output Sum,
  output CarryOut
);

  wire and_1_out, and_2_out, xor_1_out_3, xor_2_out_3;

  XOR xor_1 (.X(X), .Y(Y), .out_3(xor_1_out_3));
  XOR xor_2 (.X(X), .Y(Y), .out_3(xor_2_out_3));
  XOR xor_3 (.X(xor_2_out_3), .Y(CarryIn), .out_3(Sum));
  and and_1 (and_1_out, X, Y);
  and and_2 (and_2_out, xor_1_out_3, CarryIn);
  or or_1 (CarryOut, and_1_out, and_2_out);

  // Notes on the sheet:
  //   and outputs a 1-bit sum and a 1-bit carry-out.
  //   This is a 1-bit full adder, which takes 2 1-bit values and 1-bit carry-in as inputs
endmodule

module fulladder4 (
  input  CarryIn,
  input  [3:0] X,
  input  [3:0] Y,
  output [3:0] Sum,
  output CarryOut
);

  wire fulladder_1_carryout, fulladder_2_carryout, fulladder_3_carryout;

  fulladder fulladder_1 (.X(CarryIn), .Y(X[0]), .CarryIn(Y[0]), .Sum(Sum[0]), .CarryOut(fulladder_1_carryout));
  fulladder fulladder_2 (
    .X(fulladder_1_carryout), .Y(X[1]), .CarryIn(Y[1]), .Sum(Sum[1]), .CarryOut(fulladder_2_carryout));
  fulladder fulladder_3 (
    .X(fulladder_2_carryout), .Y(X[2]), .CarryIn(Y[2]), .Sum(Sum[2]), .CarryOut(fulladder_3_carryout));
  fulladder fulladder_4 (.X(fulladder_3_carryout), .Y(X[3]), .CarryIn(Y[3]), .Sum(Sum[3]), .CarryOut(CarryOut));

  // Notes on the sheet:
  //   and outputs a 4-bit sum and a 1-bit carryout.
  //   This is a 4-bit full adder which takes 2 4-bit values and a 1-bit carry-in as inputs
endmodule

module tester (
  input  CarryIn,
  input  [3:0] X,
  input  [1:0] Y,
  output [3:0] Sum,
  output CarryOut
);

  wire [3:0] signext2to4_1_out_2;

  signext2to4 signext2to4_1 (.in_1(Y), .out_2(signext2to4_1_out_2));
  fulladder4 fulladder4_1 (.CarryIn(CarryIn), .X(X), .Y(signext2to4_1_out_2), .Sum(Sum), .CarryOut(CarryOut));

  // Notes on the sheet:
  //   and outputs 1 4-bit sum and 1 1-bit carry-out.
  //   This is a tester of previous circuits. It takes 1 4-bit value, 12-bit value and 1 1-bit carry-in as inputs
endmodule

// signExtender
module signext2to4 (
  input  [1:0] in_1,
  output [3:0] out_2
);


  assign out_2 = {{3{in_1[1]}}, in_1[0]};

  // Notes on the sheet:
  //   This is a sign extender which extends a 2-bit 2's complement value to a 4-bit one.
endmodule
