// Logisim project alu.circ as structural Verilog: 4 circuits, main circuit main
module main (
  input  [2:0] Op_Code,
  input  [7:0] X,
  input  [7:0] Y,
  output [7:0] Output,
  output EQ,
  output OF,
  output CF,
  output ZF,
  output SF
);

  wire adder_1_cout, adder_2_cout;
  wire [0:0] comparator_1_lt;
  wire [7:0] adder_1_out, adder_2_out, and_1_out, not_1_out, or_1_out, shifter_1_out, shifter_2_out,
       shifter_3_out;

  assign not_1_out = ~Y;  // NOT_Gate not_1, 8 bits wide
  assign or_1_out = X | Y;  // OR_Gate or_1, 8 bits wide
  assign and_1_out = X & Y;  // AND_Gate and_1, 8 bits wide
  Adder adder_1 (.a(X), .b(Y), .out(adder_1_out), .cout(adder_1_cout));  // open: cin
  Adder adder_2 (.a(X), .b(not_1_out), .out(adder_2_out), .cin(1'b1), .cout(adder_2_cout));
  Shifter shifter_1 (.in(X), .\dist (Y[2:0]), .out(shifter_1_out));
  Shifter #(.shift("lr")) shifter_2 (.in(X), .\dist (Y[2:0]), .out(shifter_2_out));
  Shifter #(.shift("ar")) shifter_3 (.in(X), .\dist (Y[2:0]), .out(shifter_3_out));
  Comparator comparator_1 (.a(X), .b(Y), .eq(EQ), .lt(comparator_1_lt[0]));  // open: gt
  Multiplexer #(.select(3), .width(8), .enable("false")) multiplexer_1 (
    .in0(or_1_out), .in1(and_1_out), .in2(adder_1_out), .in3(adder_2_out), .in4(shifter_1_out),
    .in5(shifter_2_out), .in6(shifter_3_out), .in7({{7{1'b0}}, comparator_1_lt[0]}), .out(Output),
    .sel(Op_Code));
  OF of_1 (.X(X), .Y(Y), .result(Output), .op(Op_Code), .out_5(OF));
  CF cf_1 (.op_code(Op_Code), .addition_carryOut(adder_1_cout), .subtraction_carryOut(adder_2_cout), .out_4(CF));
  Comparator comparator_2 (.a({8{1'b0}}), .b(Output), .eq(ZF));  // open: gt, lt

  assign SF = Output[7];

  // Notes on the sheet:
  //   cs31 lab3, part2:alu
  //   Ziting Shen, Julian Segert
  //   This is an ALU. The input includes two 8-bit numbers and one 3-bit op code.
  //   The output is given by x op y. Additionally, the results will set values for 5 flags.
endmodule

module OF (
  input  [7:0] X,
  input  [7:0] Y,
  input  [7:0] result,
  input  [2:0] op,
  output out_5
);

  wire and_1_out, comparator_1_eq, comparator_2_eq, not_1_out, or_1_out, xor_1_out, xor_2_out;

  Comparator #(.width(3)) comparator_1 (.a(3'b010), .b(op), .eq(comparator_1_eq));  // open: gt, lt
  Comparator #(.width(3)) comparator_2 (.a(op), .b(3'b011), .eq(comparator_2_eq));  // open: gt, lt
  not not_1 (not_1_out, xor_1_out);
  xor xor_1 (xor_1_out, X[7], Y[7]);
  xor xor_2 (xor_2_out, Y[7], result[7]);
  and and_1 (and_1_out, not_1_out, xor_2_out);
  or or_1 (or_1_out, comparator_1_eq, comparator_2_eq);
  and and_2 (out_5, and_1_out, or_1_out);

  // Notes on the sheet:
  //   but the sign bit of the result is different, then the flag is set to 1.
  //   This is used to control the signed overflow flag. If the ALU is doing addition or subtraction, and the sign bits are the same,
endmodule

module CF (
  input  [2:0] op_code,
  input  addition_carryOut,
  input  subtraction_carryOut,
  output out_4
);

  wire and_1_out, and_2_out, comparator_1_eq, comparator_2_eq, not_1_out;

  Comparator #(.width(3)) comparator_1 (.a(3'b010), .b(op_code), .eq(comparator_1_eq));  // open: gt, lt
  not not_1 (not_1_out, subtraction_carryOut);
  Comparator #(.width(3)) comparator_2 (.a(op_code), .b(3'b011), .eq(comparator_2_eq));  // open: gt, lt
  and and_1 (and_1_out, comparator_1_eq, addition_carryOut);
  and and_2 (and_2_out, not_1_out, comparator_2_eq);
  or or_1 (out_4, and_1_out, and_2_out);

  // Notes on the sheet:
  //   This is used to control the unsigned overflow flag. If the ALU is doing addtion and the carry out bit of addition is 1,
  //   or if it's doing subtraction and the carry out bit of the subtraction is 0,then the flag is set to 1.
endmodule

module tester (
  input  [2:0] in_1,
  input  [7:0] in_2,
  input  [7:0] in_3,
  output [7:0] out_4,
  output out_5,
  output out_6,
  output out_7,
  output out_8,
  output out_9
);

  main main_1 (
    .Op_Code(in_1), .X(in_2), .Y(in_3), .Output(out_4), .EQ(out_6), .OF(out_9), .CF(out_8), .ZF(out_7),
    .SF(out_5));

  // Notes on the sheet:
  //   This is a tester to test the overall functions and appearance of the ALU.
endmodule
